# Fritzing sketch circuit diagram (saved by Fritzing 0.9.2b)
breadboards: 1

parts:
  Part1 = Arduino Nano (Rev3.0)
  U1 = ESP32S-HiLetgo [part_number=ESP32S-HiLetgo]
  Part2 = RFID-RC522-v2
  Part3 = RFID-RC522-v2

nets:
  GND: Part1.GND, Part2.GND
  N1: Part1.D9, Part2.RST
  N2: Part1.D10, Part2.SDA
  N3: Part1.D11/MOSI, Part2.MOSI
  N4: Part1.D12/MISO, Part2.MISO
  3V3: Part1.3V3, Part2.3.3V
  N5: Part1.D13/SCK, Part2.SCK
  N6: U1.3.3, Part3.3.3V
  GND_2: U1.GND, Part3.GND
  N7: U1.GPIO0, Part3.RST
  N8: U1.GPIO5, Part3.SDA
  N9: U1.GPIO18, Part3.SCK
  N10: U1.GPIO19, Part3.MISO
  N11: U1.GPIO23, Part3.MOSI

notes:
  [Tambah Saldo]
  [Potong Saldo]

custom parts:
  ESP32S-HiLetgo: HiLetgo ESP-WROOM-32 ESP32 ESP-32S Development Board 2.4GHz Dual-Mode WiFi + Bluetooth Dual Cores Microcontroller The ESP32 integrated with Antenna switches, RF Balun, power amplifiers, low-noise amplifiers, filters, and management modules, and the entire solution occupies the least area of PCB. 2.4 GHz Wi-Fi plus Bluetooth dual-mode chip, with TSMC Ultra-low power consumption 40nm technology,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
  RFID-RC522-v2: A simple China made RFID-RC522 Reader; do check the pin labels, as this is a MFRC522 based clone.
